# Fritzing sketch Greenhouse (saved by Fritzing 0.8.5b)
breadboards: 1

parts:
  330Ω = Resistor [tolerance=±5% resistance=220 package=THT]
  S1 = Pushbutton [package="[THT]"]
  330Ω_2 = Resistor [tolerance=±5% resistance=220 package=THT]
  LED1 = LED - 5mm [color="Red (633nm)" package="5 mm [THT]"]
  Part2 = Arduino Uno (Rev3)

nets:
  N1: 330Ω.Pin_0, 330Ω.Pin_1, S1.Pin_1, S1.Pin_2, S1.Pin_3, S1.Pin_4, 330Ω_2.Pin_1, Part2.D2, Part2.GND
  N2: 330Ω_2.Pin_0, LED1.cathode
  N3: LED1.anode, Part2.D9_PWM
